# Fritzing sketch Diagrama (saved by Fritzing 0.9.6b)

parts:
  HC-SR04_Sensor_1 = HC-SR04 Ultrasonic Distance Sensor
  Part2 = Thumb Joystick
  Part1 = Arduino Uno (Rev3)
  Keypad = Keypad Membran 4x4
  part = fc-51 [package=THT]

nets:
  VCC: HC-SR04_Sensor_1.VCC, Part2.VCC, Part1.5V, part.pin3
  N1: HC-SR04_Sensor_1.TRIG, Part1.D2
  N2: HC-SR04_Sensor_1.ECHO, Part1.D3_PWM
  GND: HC-SR04_Sensor_1.GND, Part2.GND, Part1.GND, part.pin2
  N3: Part2.SEL, Part1.D1/TX
  N4: Part2.HORZ, Part1.A1
  N5: Part2.VERT, Part1.A2
  N6: Part1.D8, Keypad.Pin4
  N7: Part1.D9_PWM, Keypad.Pin3
  N8: Part1.D10_PWM/SS, Keypad.Pin2
  N9: Part1.D11_PWM/MOSI, Keypad.Pin1
  N10: Part1.D12/MISO, part.pin1
  N11: Part1.D4, Keypad.Pin8
  N12: Part1.D5_PWM, Keypad.Pin7
  N13: Part1.D6_PWM, Keypad.Pin6
  N14: Part1.D7, Keypad.Pin5

custom parts:
  Keypad Membran 4x4: Membrane Keypad 4x4 Matrix
